// Logisim project 7MADA.circ as structural Verilog
module main (
  input  S0,
  input  S1,
  input  [4:0] A,
  input  [4:0] B,
  output C0,
  output C1,
  output C2,
  output C3,
  output C4,
  output C5,
  output C6,
  output C7,
  output out_13,
  output out_14
);

  wire addition_subtraction_1_s0, addition_subtraction_1_s1, addition_subtraction_1_s2,
       addition_subtraction_1_s3, addition_subtraction_1_s4, addition_subtraction_1_s5, and_2_out,
       division_1_c2, division_1_c3, division_1_c_sign, division_1_out_16, division_1_out_17,
       multiplyer_1_c0, multiplyer_1_c1, multiplyer_1_c2, multiplyer_1_c3, multiplyer_1_c4,
       multiplyer_1_c_sign, nor_1_out, nor_2_out, nor_3_out, nor_4_out, nor_5_out, nor_6_out, nor_7_out,
       nor_8_out, nor_9_out, nor_10_out, not_1_out, or_2_out, or_3_out, or_4_out, or_5_out, or_8_out;

  nor nor_1 (nor_1_out, B[2], nor_3_out);
  nor nor_2 (nor_2_out, B[2], nor_1_out);
  nor nor_3 (nor_3_out, B[1], B[0]);
  and and_1 (out_14, nor_2_out, and_2_out);
  not not_1 (not_1_out, S1);
  and and_2 (and_2_out, not_1_out, S0);
  Addition___Subtraction addition_subtraction_1 (
    .MO(S1), .MO_2(S0), .Sign_B(B[4]), .Sign_A(A[4]), .B3(B[3]), .A3(A[3]), .B2(B[2]), .A2(A[2]), .B1(B[1]),
    .A1(A[1]), .B0(B[0]), .A0(A[0]), .S0(addition_subtraction_1_s0), .S1(addition_subtraction_1_s1),
    .S2(addition_subtraction_1_s2), .S3(addition_subtraction_1_s3), .S4(addition_subtraction_1_s4),
    .S5(addition_subtraction_1_s5));
  multiplyer multiplyer_1 (
    .A0(A[0]), .A1(A[1]), .A2(A[2]), .A3(A[3]), .A4(A[4]), .B4(B[4]), .B3(B[2]), .B2(B[2]), .B1(B[1]),
    .B0(B[0]), .S0(S0), .S1(S1), .C_SIGN(multiplyer_1_c_sign), .C7(C7), .C6(C6), .C5(C5),
    .C4(multiplyer_1_c4), .C3(multiplyer_1_c3), .C2(multiplyer_1_c2), .C1(multiplyer_1_c1),
    .C0(multiplyer_1_c0));
  division division_1 (
    .S0(S0), .S1(S1), .C_SIGN(division_1_c_sign), .C3(division_1_c3), .C2(division_1_c2),
    .out_16(division_1_out_16), .out_17(division_1_out_17), .A4(A[4]), .A3(A[3]), .A2(A[2]), .A1(A[1]),
    .A0(A[0]), .B4(B[4]), .B3(B[2]), .B2(B[2]), .B1(B[1]), .B0(B[0]));
  or or_1 (out_13, division_1_c_sign, or_2_out);
  or or_2 (or_2_out, multiplyer_1_c_sign, addition_subtraction_1_s5);
  or or_3 (or_3_out, addition_subtraction_1_s0, multiplyer_1_c0);
  or or_4 (or_4_out, addition_subtraction_1_s2, multiplyer_1_c2);
  or or_5 (or_5_out, addition_subtraction_1_s3, multiplyer_1_c3);
  or or_6 (C4, addition_subtraction_1_s4, multiplyer_1_c4);
  or or_7 (C0, or_3_out, division_1_out_17);
  or or_8 (or_8_out, addition_subtraction_1_s1, multiplyer_1_c1);
  or or_9 (C1, or_8_out, division_1_out_16);
  or or_10 (C2, or_4_out, division_1_c2);
  or or_11 (C3, or_5_out, division_1_c3);
  nor nor_4 (nor_4_out, C1, C0);
  nor nor_5 (nor_5_out, nor_4_out, C2);
  nor nor_6 (nor_6_out, nor_5_out, C3);
  nor nor_7 (nor_7_out, C5, nor_9_out);
  nor nor_8 (nor_8_out, C7, nor_10_out);
  nor nor_9 (nor_9_out, nor_6_out, C4);
  nor nor_10 (nor_10_out, nor_7_out, C6);
endmodule

module _1_1_bit_comparetor (
  input  A,
  input  B,
  output LARGER,
  output SMALLER,
  output Equal
);

  wire and_3_out, and_4_out, not_1_out, not_2_out;

  not not_1 (not_1_out, A);
  not not_2 (not_2_out, B);
  and and_1 (LARGER, A, not_2_out);
  and and_2 (SMALLER, not_1_out, B);
  and and_3 (and_3_out, not_1_out, not_2_out);
  and and_4 (and_4_out, A, B);
  or or_1 (Equal, and_3_out, and_4_out);
endmodule

module _4_bit_comparetor (
  input  a3,
  input  a2,
  input  a1,
  input  a0,
  input  b3,
  input  b2,
  input  b1,
  input  b0,
  output Larger,
  output Smaller,
  output Equal
);

  wire and_1_out, and_2_out, and_3_out, and_4_out, and_5_out, and_6_out, n1_1_bit_comparetor_1_equal,
       n1_1_bit_comparetor_1_larger, n1_1_bit_comparetor_1_smaller, n1_1_bit_comparetor_2_equal,
       n1_1_bit_comparetor_2_larger, n1_1_bit_comparetor_2_smaller, n1_1_bit_comparetor_3_equal,
       n1_1_bit_comparetor_3_larger, n1_1_bit_comparetor_3_smaller, n1_1_bit_comparetor_4_equal,
       n1_1_bit_comparetor_4_larger, n1_1_bit_comparetor_4_smaller;

  _1_1_bit_comparetor u_1_1_bit_comparetor_1 (
    .A(a3), .B(b3), .LARGER(n1_1_bit_comparetor_1_larger), .SMALLER(n1_1_bit_comparetor_1_smaller),
    .Equal(n1_1_bit_comparetor_1_equal));
  _1_1_bit_comparetor u_1_1_bit_comparetor_2 (
    .A(a2), .B(b2), .LARGER(n1_1_bit_comparetor_2_larger), .SMALLER(n1_1_bit_comparetor_2_smaller),
    .Equal(n1_1_bit_comparetor_2_equal));
  _1_1_bit_comparetor u_1_1_bit_comparetor_3 (
    .A(a1), .B(b1), .LARGER(n1_1_bit_comparetor_3_larger), .SMALLER(n1_1_bit_comparetor_3_smaller),
    .Equal(n1_1_bit_comparetor_3_equal));
  _1_1_bit_comparetor u_1_1_bit_comparetor_4 (
    .A(a0), .B(b0), .LARGER(n1_1_bit_comparetor_4_larger), .SMALLER(n1_1_bit_comparetor_4_smaller),
    .Equal(n1_1_bit_comparetor_4_equal));
  and and_1 (and_1_out, n1_1_bit_comparetor_2_larger, n1_1_bit_comparetor_1_equal);
  and and_2 (and_2_out, n1_1_bit_comparetor_1_equal, n1_1_bit_comparetor_2_equal, n1_1_bit_comparetor_3_larger);
  and and_3 (and_3_out, n1_1_bit_comparetor_1_equal, n1_1_bit_comparetor_2_equal, n1_1_bit_comparetor_3_equal, n1_1_bit_comparetor_4_larger);
  and and_4 (and_4_out, n1_1_bit_comparetor_1_equal, n1_1_bit_comparetor_2_smaller);
  and and_5 (and_5_out, n1_1_bit_comparetor_1_equal, n1_1_bit_comparetor_2_equal, n1_1_bit_comparetor_3_smaller);
  and and_6 (and_6_out, n1_1_bit_comparetor_1_equal, n1_1_bit_comparetor_2_equal, n1_1_bit_comparetor_3_equal, n1_1_bit_comparetor_4_smaller);
  and and_7 (Equal, n1_1_bit_comparetor_1_equal, n1_1_bit_comparetor_2_equal, n1_1_bit_comparetor_3_equal, n1_1_bit_comparetor_4_equal);
  or or_1 (Larger, n1_1_bit_comparetor_1_larger, and_1_out, and_2_out, and_3_out);
  or or_2 (Smaller, n1_1_bit_comparetor_1_smaller, and_4_out, and_5_out, and_6_out);
endmodule

module division (
  input  S0,
  input  S1,
  input  A4,
  input  A3,
  input  A2,
  input  A1,
  input  A0,
  input  B4,
  input  B3,
  input  B2,
  input  B1,
  input  B0,
  output C_SIGN,
  output C3,
  output C2,
  output out_16,
  output out_17
);

  wire and_1_out, and_6_out, division_multiplication_1_c0, division_multiplication_2_c0,
       division_multiplication_2_c1, division_multiplication_3_c0, division_multiplication_3_c1,
       division_multiplication_3_c2, division_subtraction_1_c3, division_subtraction_2_c0,
       division_subtraction_2_c1, division_subtraction_2_c2, division_subtraction_2_c3,
       division_subtraction_3_c1, division_subtraction_3_c2, division_subtraction_3_c3,
       n4_bit_comp_number_2_1_greater_or_equal, n4_bit_comp_number_2_2_greater_or_equal,
       n4_bit_comp_number_2_3_greater_or_equal, n4_bit_comp_number_2_4_greater_or_equal, nor_1_out,
       nor_2_out, nor_3_out, not_1_out, not_2_out, xor_1_out;

  _4_bit_comp_number_2 u_4_bit_comp_number_2_1 (
    .a3(1'b0), .a2(1'b0), .a1(1'b0), .a0(A3), .b3(B3), .b2(B2), .b1(B1), .b0(B0),
    .GREATER_OR_EQUAL(n4_bit_comp_number_2_1_greater_or_equal));
  Division_multiplication division_multiplication_1 (
    .A(n4_bit_comp_number_2_1_greater_or_equal), .B3(B3), .B2(B2), .B1(B1), .B0(B0),
    .C0(division_multiplication_1_c0));  // open: C3, C2, C1
  _4_bit_comp_number_2 u_4_bit_comp_number_2_2 (
    .a3(1'b0), .a2(1'b0), .a1(division_subtraction_1_c3), .a0(A2), .b3(B3), .b2(B2), .b1(B1), .b0(B0),
    .GREATER_OR_EQUAL(n4_bit_comp_number_2_2_greater_or_equal));
  _4_bit_comp_number_2 u_4_bit_comp_number_2_3 (
    .a3(1'b0), .a2(division_subtraction_2_c3), .a1(division_subtraction_2_c2), .a0(A1), .b3(B3), .b2(B2),
    .b1(B1), .b0(B0), .GREATER_OR_EQUAL(n4_bit_comp_number_2_3_greater_or_equal));
  _4_bit_comp_number_2 u_4_bit_comp_number_2_4 (
    .a3(division_subtraction_3_c3), .a2(division_subtraction_3_c2), .a1(division_subtraction_3_c1), .a0(A0),
    .b3(B3), .b2(B2), .b1(B1), .b0(B0), .GREATER_OR_EQUAL(n4_bit_comp_number_2_4_greater_or_equal));
  DIVISION_SUBTRACTION division_subtraction_1 (
    .b3(division_multiplication_1_c0), .a3(A3), .b2(1'b0), .a2(1'b0), .b1(1'b0), .a1(1'b0), .b0(1'b0),
    .a0(1'b0), .C3(division_subtraction_1_c3));  // open: C2, C1, C0
  Division_multiplication division_multiplication_2 (
    .A(n4_bit_comp_number_2_2_greater_or_equal), .B3(B3), .B2(B2), .B1(B1), .B0(B0),
    .C1(division_multiplication_2_c1), .C0(division_multiplication_2_c0));  // open: C3, C2
  Division_multiplication division_multiplication_3 (
    .A(n4_bit_comp_number_2_3_greater_or_equal), .B3(B3), .B2(B2), .B1(B1), .B0(B0),
    .C2(division_multiplication_3_c2), .C1(division_multiplication_3_c1), .C0(division_multiplication_3_c0));  // open: C3
  DIVISION_SUBTRACTION division_subtraction_2 (
    .b3(division_multiplication_2_c1), .a3(division_subtraction_1_c3), .b2(division_multiplication_2_c0),
    .a2(A2), .b1(1'b0), .a1(1'b0), .b0(1'b0), .a0(1'b0), .C3(division_subtraction_2_c3),
    .C2(division_subtraction_2_c2), .C1(division_subtraction_2_c1), .C0(division_subtraction_2_c0));
  DIVISION_SUBTRACTION division_subtraction_3 (
    .b3(division_multiplication_3_c2), .a3(division_subtraction_2_c3), .b2(division_multiplication_3_c1),
    .a2(division_subtraction_2_c2), .b1(division_multiplication_3_c0), .a1(A1), .b0(1'b0), .a0(1'b0),
    .C3(division_subtraction_3_c3), .C2(division_subtraction_3_c2), .C1(division_subtraction_3_c1));  // open: C0
  not not_1 (not_1_out, S1);
  and and_1 (and_1_out, not_1_out, S0);
  xor xor_1 (xor_1_out, B4, A4);
  and and_2 (C3, n4_bit_comp_number_2_1_greater_or_equal, and_1_out);
  and and_3 (C2, n4_bit_comp_number_2_2_greater_or_equal, and_1_out);
  and and_4 (out_16, n4_bit_comp_number_2_3_greater_or_equal, and_1_out);
  and and_5 (out_17, n4_bit_comp_number_2_4_greater_or_equal, and_1_out);
  and and_6 (and_6_out, xor_1_out, and_1_out);
  nor nor_1 (nor_1_out, B0, B1);
  not not_2 (not_2_out, nor_3_out);
  nor nor_2 (nor_2_out, nor_1_out, B2);
  and and_7 (C_SIGN, and_6_out, not_2_out);
  nor nor_3 (nor_3_out, nor_2_out, B3);
endmodule

module _4_bit_comp_number_2 (
  input  a3,
  input  a2,
  input  a1,
  input  a0,
  input  b3,
  input  b2,
  input  b1,
  input  b0,
  output GREATER_OR_EQUAL
);

  wire and_1_out, and_2_out, and_3_out, and_4_out, n1_1_bit_comparetor_1_equal, n1_1_bit_comparetor_1_larger,
       n1_1_bit_comparetor_1_smaller, n1_1_bit_comparetor_2_equal, n1_1_bit_comparetor_2_larger,
       n1_1_bit_comparetor_2_smaller, n1_1_bit_comparetor_3_equal, n1_1_bit_comparetor_3_larger,
       n1_1_bit_comparetor_3_smaller, n1_1_bit_comparetor_4_equal, n1_1_bit_comparetor_4_larger,
       n1_1_bit_comparetor_4_smaller, or_1_out;

  _1_1_bit_comparetor u_1_1_bit_comparetor_1 (
    .A(a3), .B(b3), .LARGER(n1_1_bit_comparetor_1_larger), .SMALLER(n1_1_bit_comparetor_1_smaller),
    .Equal(n1_1_bit_comparetor_1_equal));
  _1_1_bit_comparetor u_1_1_bit_comparetor_2 (
    .A(a2), .B(b2), .LARGER(n1_1_bit_comparetor_2_larger), .SMALLER(n1_1_bit_comparetor_2_smaller),
    .Equal(n1_1_bit_comparetor_2_equal));
  _1_1_bit_comparetor u_1_1_bit_comparetor_3 (
    .A(a1), .B(b1), .LARGER(n1_1_bit_comparetor_3_larger), .SMALLER(n1_1_bit_comparetor_3_smaller),
    .Equal(n1_1_bit_comparetor_3_equal));
  _1_1_bit_comparetor u_1_1_bit_comparetor_4 (
    .A(a0), .B(b0), .LARGER(n1_1_bit_comparetor_4_larger), .SMALLER(n1_1_bit_comparetor_4_smaller),
    .Equal(n1_1_bit_comparetor_4_equal));
  and and_1 (and_1_out, n1_1_bit_comparetor_1_equal, n1_1_bit_comparetor_2_larger);
  and and_2 (and_2_out, n1_1_bit_comparetor_1_equal, n1_1_bit_comparetor_2_equal, n1_1_bit_comparetor_3_larger);
  and and_3 (and_3_out, n1_1_bit_comparetor_1_equal, n1_1_bit_comparetor_2_equal, n1_1_bit_comparetor_3_equal, n1_1_bit_comparetor_4_larger);
  and and_4 (and_4_out, n1_1_bit_comparetor_1_equal, n1_1_bit_comparetor_2_equal, n1_1_bit_comparetor_3_equal, n1_1_bit_comparetor_4_equal);
  or or_1 (or_1_out, n1_1_bit_comparetor_1_larger, and_1_out, and_2_out, and_3_out);
  or or_2 (GREATER_OR_EQUAL, or_1_out, and_4_out);
endmodule

module half_adder (
  input  a,
  input  b,
  output sum,
  output carry
);

  xor xor_1 (sum, a, b);
  and and_1 (carry, a, b);
endmodule

module full_adder (
  input  a,
  input  b,
  input  c,
  output sum,
  output carry
);

  wire half_adder_1_carry, half_adder_1_sum, half_adder_2_carry;

  half_adder half_adder_1 (.a(a), .b(b), .sum(half_adder_1_sum), .carry(half_adder_1_carry));
  half_adder half_adder_2 (.a(half_adder_1_sum), .b(c), .sum(sum), .carry(half_adder_2_carry));
  or or_1 (carry, half_adder_1_carry, half_adder_2_carry);
endmodule

module _5_bit_adder (
  input  a4,
  input  a3,
  input  a2,
  input  a1,
  input  a0,
  input  b4,
  input  b3,
  input  b2,
  input  b1,
  input  b0,
  output c5,
  output c4,
  output c3,
  output c2,
  output c1,
  output c0
);

  wire full_adder_1_carry, full_adder_2_carry, full_adder_3_carry, full_adder_4_carry;

  full_adder full_adder_1 (.a(a0), .b(b0), .c(1'b0), .sum(c0), .carry(full_adder_1_carry));
  full_adder full_adder_2 (.a(a1), .b(b1), .c(full_adder_1_carry), .sum(c1), .carry(full_adder_2_carry));
  full_adder full_adder_3 (.a(a2), .b(b2), .c(full_adder_2_carry), .sum(c2), .carry(full_adder_3_carry));
  full_adder full_adder_4 (.a(a3), .b(b3), .c(full_adder_3_carry), .sum(c3), .carry(full_adder_4_carry));
  full_adder full_adder_5 (.a(a4), .b(b4), .c(full_adder_4_carry), .sum(c4), .carry(c5));
endmodule

module _5_bit_subtractor (
  input  b4,
  input  a4,
  input  b3,
  input  a3,
  input  b2,
  input  a2,
  input  b1,
  input  a1,
  input  b0,
  input  a0,
  output out_11,
  output out_12,
  output out_13,
  output out_14,
  output out_15
);

  wire full_adder_2_carry, full_adder_3_carry, full_adder_4_carry, full_adder_5_carry, not_1_out, not_2_out,
       not_3_out, not_4_out, not_5_out, not_6_out;

  not not_1 (not_1_out, b4);
  full_adder full_adder_1 (.a(a4), .b(not_1_out), .c(full_adder_2_carry), .sum(out_11));  // open: carry
  not not_2 (not_2_out, b3);
  full_adder full_adder_2 (.a(a3), .b(not_2_out), .c(full_adder_3_carry), .sum(out_12), .carry(full_adder_2_carry));
  not not_3 (not_3_out, b2);
  full_adder full_adder_3 (.a(a2), .b(not_3_out), .c(full_adder_4_carry), .sum(out_13), .carry(full_adder_3_carry));
  not not_4 (not_4_out, b1);
  full_adder full_adder_4 (.a(a1), .b(not_4_out), .c(full_adder_5_carry), .sum(out_14), .carry(full_adder_4_carry));
  not not_5 (not_5_out, b0);
  full_adder full_adder_5 (.a(a0), .b(not_5_out), .c(not_6_out), .sum(out_15), .carry(full_adder_5_carry));
  not not_6 (not_6_out, 1'b0);
endmodule

module multiplyer (
  input  B4,
  input  B3,
  input  B2,
  input  B1,
  input  B0,
  input  A0,
  input  S0,
  input  S1,
  input  A1,
  input  A2,
  input  A3,
  input  A4,
  output C0,
  output C4,
  output C3,
  output C2,
  output C7,
  output C6,
  output C1,
  output C5,
  output C_SIGN
);

  wire and_2_out, and_3_out, and_4_out, and_5_out, and_7_out, and_8_out, and_9_out, and_10_out, and_11_out,
       and_12_out, and_14_out, and_15_out, and_16_out, and_18_out, and_20_out, and_22_out, and_25_out,
       and_27_out, n5_bit_adder_1_c0, n5_bit_adder_1_c1, n5_bit_adder_1_c2, n5_bit_adder_1_c3,
       n5_bit_adder_1_c4, n5_bit_adder_2_c0, n5_bit_adder_2_c1, n5_bit_adder_2_c2, n5_bit_adder_2_c3,
       n5_bit_adder_2_c4, n5_bit_adder_3_c0, n5_bit_adder_3_c1, n5_bit_adder_3_c2, n5_bit_adder_3_c3,
       n5_bit_adder_3_c4, nor_1_out, nor_2_out, nor_3_out, not_1_out, not_2_out, xor_1_out;

  not not_1 (not_1_out, nor_1_out);
  and and_1 (C_SIGN, not_1_out, and_2_out);
  xor xor_1 (xor_1_out, A4, B4);
  and and_2 (and_2_out, and_27_out, xor_1_out);
  and and_3 (and_3_out, A1, B3);
  and and_4 (and_4_out, A2, B3);
  and and_5 (and_5_out, A3, B3);
  and and_6 (C7, and_27_out, n5_bit_adder_1_c4);
  and and_7 (and_7_out, A1, B2);
  and and_8 (and_8_out, A2, B2);
  and and_9 (and_9_out, A3, B2);
  _5_bit_adder u_5_bit_adder_1 (
    .a4(1'b0), .b4(1'b0), .a3(and_5_out), .b3(n5_bit_adder_3_c4), .b2(n5_bit_adder_3_c3), .a2(and_9_out),
    .b1(and_12_out), .a1(n5_bit_adder_3_c2), .b0(and_16_out), .a0(n5_bit_adder_3_c1), .c4(n5_bit_adder_1_c4),
    .c3(n5_bit_adder_1_c3), .c2(n5_bit_adder_1_c2), .c1(n5_bit_adder_1_c1), .c0(n5_bit_adder_1_c0));  // open: c5
  and and_10 (and_10_out, A1, B1);
  _5_bit_adder u_5_bit_adder_2 (
    .a4(1'b0), .b4(1'b0), .a3(and_3_out), .b3(1'b0), .b2(and_14_out), .a2(and_7_out), .b1(and_10_out),
    .a1(and_20_out), .b0(and_18_out), .a0(and_22_out), .c4(n5_bit_adder_2_c4), .c3(n5_bit_adder_2_c3),
    .c2(n5_bit_adder_2_c2), .c1(n5_bit_adder_2_c1), .c0(n5_bit_adder_2_c0));  // open: c5
  and and_11 (and_11_out, A2, B1);
  _5_bit_adder u_5_bit_adder_3 (
    .a4(1'b0), .b4(1'b0), .a3(and_4_out), .b3(n5_bit_adder_2_c4), .b2(n5_bit_adder_2_c3), .a2(and_8_out),
    .b1(and_11_out), .a1(n5_bit_adder_2_c2), .b0(and_15_out), .a0(n5_bit_adder_2_c1), .c4(n5_bit_adder_3_c4),
    .c3(n5_bit_adder_3_c3), .c2(n5_bit_adder_3_c2), .c1(n5_bit_adder_3_c1), .c0(n5_bit_adder_3_c0));  // open: c5
  and and_12 (and_12_out, A3, B1);
  and and_13 (C6, and_27_out, n5_bit_adder_1_c3);
  and and_14 (and_14_out, A0, B3);
  and and_15 (and_15_out, A2, B0);
  and and_16 (and_16_out, A3, B0);
  and and_17 (C5, and_27_out, n5_bit_adder_1_c2);
  and and_18 (and_18_out, A1, B0);
  and and_19 (C4, and_27_out, n5_bit_adder_1_c1);
  and and_20 (and_20_out, A0, B2);
  and and_21 (C3, and_27_out, n5_bit_adder_1_c0);
  and and_22 (and_22_out, A0, B1);
  and and_23 (C2, and_27_out, n5_bit_adder_3_c0);
  and and_24 (C1, and_27_out, and_27_out);
  and and_25 (and_25_out, A0, B0);
  and and_26 (C0, and_25_out, and_27_out);
  not not_2 (not_2_out, S0);
  and and_27 (and_27_out, not_2_out, S1);
  nor nor_1 (nor_1_out, B3, nor_2_out);
  nor nor_2 (nor_2_out, B2, nor_3_out);
  nor nor_3 (nor_3_out, B1, B0);
endmodule

module circuit (
  input  in_1,
  input  in_2,
  input  in_3,
  input  in_4
);

  wire not_1_out, not_2_out, not_3_out, not_4_out;

  not not_1 (not_1_out, in_1);
  not not_2 (not_2_out, in_2);
  not not_3 (not_3_out, in_3);
  not not_4 (not_4_out, in_4);
  // AND_Gate ABAR_C has open pins: in0=in_3, in1=not_1_out, out=open
  // AND_Gate and_1 has open pins: in0=not_1_out, in1=in_2, out=open
  // AND_Gate and_2 is placed but not wired
  // AND_Gate and_3 is placed but not wired
  // AND_Gate and_4 is placed but not wired
endmodule

module Division_multiplication (
  input  B3,
  input  B2,
  input  B1,
  input  B0,
  input  A,
  output C3,
  output C2,
  output C1,
  output C0
);

  and and_1 (C3, A, B3);
  and and_2 (C2, A, B2);
  and and_3 (C1, A, B1);
  and and_4 (C0, A, B0);
endmodule

module DIVISION_SUBTRACTION (
  input  b3,
  input  a3,
  input  b2,
  input  a2,
  input  b1,
  input  a1,
  input  b0,
  input  a0,
  output C3,
  output C2,
  output C1,
  output C0
);

  wire full_adder_2_carry, full_adder_3_carry, full_adder_4_carry, not_1_out, not_2_out, not_3_out,
       not_4_out, not_5_out;

  not not_1 (not_1_out, b3);
  full_adder full_adder_1 (.a(a3), .b(not_1_out), .c(full_adder_2_carry), .sum(C3));  // open: carry
  not not_2 (not_2_out, b2);
  full_adder full_adder_2 (.a(a2), .b(not_2_out), .c(full_adder_3_carry), .sum(C2), .carry(full_adder_2_carry));
  not not_3 (not_3_out, b1);
  full_adder full_adder_3 (.a(a1), .b(not_3_out), .c(full_adder_4_carry), .sum(C1), .carry(full_adder_3_carry));
  not not_4 (not_4_out, b0);
  full_adder full_adder_4 (.a(a0), .b(not_4_out), .c(not_5_out), .sum(C0), .carry(full_adder_4_carry));
  not not_5 (not_5_out, 1'b0);
endmodule

module _7_segment (
  input  x3,
  input  x2,
  input  x1,
  input  x0,
  output a,
  output b,
  output c,
  output d,
  output e,
  output f,
  output g
);

  wire and_1_out, and_2_out, and_3_out, and_4_out, and_5_out, and_6_out, and_7_out, and_8_out, and_9_out,
       not_1_out, not_2_out, not_3_out, not_4_out, or_1_out, or_2_out, or_3_out, or_4_out, or_6_out,
       or_7_out, or_8_out, or_12_out, or_13_out, or_14_out, or_15_out;

  not not_1 (not_1_out, x3);
  not not_2 (not_2_out, x2);
  not not_3 (not_3_out, x1);
  not not_4 (not_4_out, x0);
  and and_1 (and_1_out, x2, not_3_out);
  and and_2 (and_2_out, x2, not_4_out);
  and and_3 (and_3_out, x2, x0);
  and and_4 (and_4_out, not_2_out, not_4_out);
  and and_5 (and_5_out, x1, x0);
  and and_6 (and_6_out, not_3_out, not_4_out);
  and and_7 (and_7_out, x1, not_4_out);
  and and_8 (and_8_out, not_2_out, x1);
  and and_9 (and_9_out, x0, and_1_out);
  or or_1 (or_1_out, and_3_out, and_4_out);
  or or_2 (or_2_out, and_5_out, and_6_out);
  or or_3 (or_3_out, x2, not_3_out);
  or or_4 (or_4_out, and_7_out, and_8_out);
  or or_5 (e, and_7_out, and_4_out);
  or or_6 (or_6_out, and_1_out, and_2_out);
  or or_7 (or_7_out, and_1_out, and_8_out);
  or or_8 (or_8_out, or_1_out, x3);
  or or_9 (b, or_2_out, not_2_out);
  or or_10 (a, or_8_out, x1);
  or or_11 (c, or_3_out, x0);
  or or_12 (or_12_out, or_4_out, x3);
  or or_13 (or_13_out, or_12_out, and_9_out);
  or or_14 (or_14_out, or_6_out, x3);
  or or_15 (or_15_out, or_7_out, x3);
  or or_16 (d, or_13_out, and_4_out);
  or or_17 (f, or_14_out, and_6_out);
  or or_18 (g, or_15_out, and_7_out);
endmodule

module test (
  input  in_1,
  input  in_2,
  input  in_3,
  input  in_4,
  input  in_5,
  input  in_6,
  input  in_7,
  input  in_8,
  input  in_9,
  input  in_10,
  input  in_11,
  input  in_12
);

  wire binary_to_bcd_1_p0, binary_to_bcd_1_p1, binary_to_bcd_1_p2, binary_to_bcd_1_p3, binary_to_bcd_1_p4,
       binary_to_bcd_1_p5, binary_to_bcd_1_p6, binary_to_bcd_1_p7, binary_to_bcd_1_p8, binary_to_bcd_1_p9,
       binary_to_bcd_1_p10, binary_to_bcd_1_p11, main_1_p12, main_1_p13, main_1_p15, main_1_p16, main_1_p17,
       main_1_p18, main_1_p19, main_1_p20, main_1_p21, main_1_p22, main_1_p23, n7_segment_1_a,
       n7_segment_1_b, n7_segment_1_c, n7_segment_1_d, n7_segment_1_e, n7_segment_1_f, n7_segment_1_g,
       n7_segment_2_a, n7_segment_2_b, n7_segment_2_c, n7_segment_2_d, n7_segment_2_e, n7_segment_2_f,
       n7_segment_2_g, n7_segment_3_a, n7_segment_3_b, n7_segment_3_c, n7_segment_3_d, n7_segment_3_e,
       n7_segment_3_f, n7_segment_3_g;

  LED led_1 (.in(main_1_p12));
  LED led_2 (.in(main_1_p13));
  // main main_1: pin names not known; wires that end beside it: in_1, in_2, in_3, in_4, in_7, in_8, in_9, in_10, in_11, in_12, in_5, main_1_p12, main_1_p13, in_6, main_1_p15, main_1_p16, main_1_p17, main_1_p18, main_1_p19, main_1_p20, main_1_p21, main_1_p22, main_1_p23, main_1_p23
  Binary_To_BCD binary_to_bcd_1 (
    .B7(main_1_p23), .B6(main_1_p22), .B5(main_1_p21), .B4(main_1_p20), .B3(main_1_p19), .B2(main_1_p18),
    .B1(main_1_p17), .B0(main_1_p16), .P11(binary_to_bcd_1_p11), .P10(binary_to_bcd_1_p10),
    .P9(binary_to_bcd_1_p9), .P8(binary_to_bcd_1_p8), .P7(binary_to_bcd_1_p7), .P6(binary_to_bcd_1_p6),
    .P5(binary_to_bcd_1_p5), .P4(binary_to_bcd_1_p4), .P3(binary_to_bcd_1_p3), .P2(binary_to_bcd_1_p2),
    .P1(binary_to_bcd_1_p1), .P0(binary_to_bcd_1_p0));
  LED led_3 (.in(main_1_p15));
  _7_Segment_Display u_7_segment_display_1 (
    .g(n7_segment_1_g), .f(n7_segment_1_f), .a(n7_segment_1_a), .b(n7_segment_1_b), .e(n7_segment_1_e),
    .d(n7_segment_1_d), .c(n7_segment_1_c));  // open: dp
  _7_segment u_7_segment_1 (
    .a(n7_segment_1_a), .b(n7_segment_1_b), .c(n7_segment_1_c), .d(n7_segment_1_d), .e(n7_segment_1_e),
    .f(n7_segment_1_f), .g(n7_segment_1_g), .x3(binary_to_bcd_1_p11), .x2(binary_to_bcd_1_p10),
    .x1(binary_to_bcd_1_p9), .x0(binary_to_bcd_1_p8));
  _7_Segment_Display u_7_segment_display_2 (
    .g(n7_segment_2_g), .f(n7_segment_2_f), .a(n7_segment_2_a), .b(n7_segment_2_b), .e(n7_segment_2_e),
    .d(n7_segment_2_d), .c(n7_segment_2_c));  // open: dp
  _7_segment u_7_segment_2 (
    .a(n7_segment_2_a), .b(n7_segment_2_b), .c(n7_segment_2_c), .d(n7_segment_2_d), .e(n7_segment_2_e),
    .f(n7_segment_2_f), .g(n7_segment_2_g), .x3(binary_to_bcd_1_p7), .x2(binary_to_bcd_1_p6),
    .x1(binary_to_bcd_1_p5), .x0(binary_to_bcd_1_p4));
  _7_segment u_7_segment_3 (
    .a(n7_segment_3_a), .b(n7_segment_3_b), .c(n7_segment_3_c), .d(n7_segment_3_d), .e(n7_segment_3_e),
    .f(n7_segment_3_f), .g(n7_segment_3_g), .x3(binary_to_bcd_1_p3), .x2(binary_to_bcd_1_p2),
    .x1(binary_to_bcd_1_p1), .x0(binary_to_bcd_1_p0));
  _7_Segment_Display u_7_segment_display_3 (
    .g(n7_segment_3_g), .f(n7_segment_3_f), .a(n7_segment_3_a), .b(n7_segment_3_b), .e(n7_segment_3_e),
    .d(n7_segment_3_d), .c(n7_segment_3_c));  // open: dp

  // Notes on the sheet:
  //   00 ADD
  //                 01 subtraction
  //                     11 multiplication
  //                  10 division
endmodule

module C (
  input  A3,
  input  A2,
  input  A1,
  input  A0,
  output S3,
  output S2,
  output S1,
  output S0
);

  wire and_1_out, and_2_out, and_3_out, and_4_out, and_5_out, and_6_out, and_7_out, and_8_out, and_9_out,
       and_10_out, and_11_out, and_12_out, and_13_out, and_14_out, and_15_out, not_1_out, not_2_out,
       not_3_out, not_4_out, or_1_out, or_3_out, or_4_out;

  not not_1 (not_1_out, A3);
  not not_2 (not_2_out, A2);
  not not_3 (not_3_out, A1);
  not not_4 (not_4_out, A0);
  and and_1 (and_1_out, A0, A2);
  and and_2 (and_2_out, A2, A1);
  and and_3 (and_3_out, not_1_out, not_2_out);
  and and_4 (and_4_out, and_2_out, not_4_out);
  and and_5 (and_5_out, A3, not_3_out);
  and and_6 (and_6_out, A2, A0);
  and and_7 (and_7_out, A1, A2);
  and and_8 (and_8_out, A1, and_1_out);
  and and_9 (and_9_out, A2, not_3_out);
  and and_10 (and_10_out, A3, A0);
  and and_11 (and_11_out, A3, not_4_out);
  and and_12 (and_12_out, not_2_out, A1);
  and and_13 (and_13_out, and_3_out, A0);
  and and_14 (and_14_out, A3, not_4_out);
  or or_1 (or_1_out, and_5_out, and_6_out);
  and and_15 (and_15_out, not_4_out, and_9_out);
  or or_2 (S3, or_1_out, and_7_out);
  or or_3 (or_3_out, and_11_out, and_12_out);
  or or_4 (or_4_out, and_13_out, and_14_out);
  or or_5 (S2, and_15_out, and_10_out);
  or or_6 (S1, or_3_out, and_8_out);
  or or_7 (S0, or_4_out, and_4_out);
endmodule

module Binary_To_BCD (
  input  B7,
  input  B6,
  input  B5,
  input  B4,
  input  B3,
  input  B2,
  input  B1,
  input  B0,
  output P11,
  output P10,
  output P9,
  output P8,
  output P7,
  output P6,
  output P5,
  output P4,
  output P3,
  output P2,
  output P1,
  output P0
);

  wire c_1_s0, c_1_s1, c_1_s2, c_1_s3, c_2_s0, c_2_s1, c_2_s2, c_3_s0, c_3_s1, c_3_s2, c_3_s3, c_4_s0,
       c_4_s1, c_4_s2, c_4_s3, c_6_s0, c_6_s1, c_6_s2, c_6_s3;

  C c_1 (.A3(1'b0), .A2(B7), .A1(B6), .A0(B5), .S3(c_1_s3), .S2(c_1_s2), .S1(c_1_s1), .S0(c_1_s0));
  C c_2 (.A3(1'b0), .A2(c_1_s3), .A1(c_3_s3), .A0(c_4_s3), .S3(P9), .S2(c_2_s2), .S1(c_2_s1), .S0(c_2_s0));
  C c_3 (.A3(c_1_s2), .A2(c_1_s1), .A1(c_1_s0), .A0(B4), .S3(c_3_s3), .S2(c_3_s2), .S1(c_3_s1), .S0(c_3_s0));
  C c_4 (.A3(c_3_s2), .A2(c_3_s1), .A1(c_3_s0), .A0(B3), .S3(c_4_s3), .S2(c_4_s2), .S1(c_4_s1), .S0(c_4_s0));
  C c_5 (.A3(c_2_s2), .A2(c_2_s1), .A1(c_2_s0), .A0(c_6_s3), .S3(P8), .S2(P7), .S1(P6), .S0(P5));
  C c_6 (.A3(c_4_s2), .A2(c_4_s1), .A1(c_4_s0), .A0(B2), .S3(c_6_s3), .S2(c_6_s2), .S1(c_6_s1), .S0(c_6_s0));
  C c_7 (.A3(c_6_s2), .A2(c_6_s1), .A1(c_6_s0), .A0(B1), .S3(P4), .S2(P3), .S1(P2), .S0(P1));

  assign P0 = B0;
  assign P10 = 1'b0;
  assign P11 = 1'b0;
endmodule

module fsfs (
);

  division division_1 ();  // open: S0, S1, C_SIGN, C3, C2, out_16, out_17, A4, A3, A2, A1, A0, B4, B3, B2, B1, B0
  multiplyer multiplyer_1 ();  // open: A0, A1, A2, A3, A4, B4, B3, B2, B1, B0, S0, S1, C_SIGN, C7, C6, C5, C4, C3, C2, C1, C0
endmodule

module Addition___Subtraction (
  input  MO,
  input  MO_2,
  input  Sign_B,
  input  Sign_A,
  input  B3,
  input  A3,
  input  B2,
  input  A2,
  input  B1,
  input  A1,
  input  B0,
  input  A0,
  output S0,
  output S1,
  output S2,
  output S3,
  output S4,
  output S5
);

  wire and_1_out, and_2_out, and_3_out, and_4_out, full_adder_1_carry, full_adder_1_sum, full_adder_2_carry,
       full_adder_2_sum, full_adder_3_carry, full_adder_3_sum, full_adder_4_carry, full_adder_4_sum,
       half_adder_1_carry, half_adder_1_sum, half_adder_2_carry, half_adder_2_sum, half_adder_3_carry,
       half_adder_3_sum, half_adder_4_carry, half_adder_4_sum, mux_1_z, mux_2_z, mux_3_z, mux_4_z, mux_5_z,
       mux_6_z, not_1_out, not_2_out, not_3_out, or_1_out, or_2_out, or_3_out, or_4_out, or_5_out, or_6_out,
       xor_1_out, xor_2_out, xor_3_out, xor_4_out, xor_5_out, xor_6_out, xor_7_out, xor_8_out, xor_9_out,
       xor_10_out, xor_11_out, xor_12_out, xor_13_out, xor_14_out;

  and and_1 (and_1_out, MO, MO_2);
  xor xor_1 (xor_1_out, and_2_out, B3);
  not not_1 (not_1_out, full_adder_1_carry);
  xor xor_2 (xor_2_out, and_1_out, Sign_B);
  xor xor_3 (xor_3_out, and_3_out, A3);
  Full_Adder full_adder_1 (
    .X(xor_3_out), .Y(xor_1_out), .Z(full_adder_2_carry), .Sum(full_adder_1_sum), .Carry(full_adder_1_carry));
  mux mux_1 (.I0(Sign_A), .I1(not_1_out), .sign(xor_4_out), .z(mux_1_z));
  xor xor_4 (xor_4_out, xor_2_out, Sign_A);
  xor xor_5 (xor_5_out, and_2_out, B2);
  xor xor_6 (xor_6_out, full_adder_1_sum, not_1_out);
  and and_2 (and_2_out, xor_2_out, xor_4_out);
  and and_3 (and_3_out, xor_4_out, Sign_A);
  xor xor_7 (xor_7_out, and_3_out, A2);
  Full_Adder full_adder_2 (
    .X(xor_7_out), .Y(xor_5_out), .Z(full_adder_3_carry), .Sum(full_adder_2_sum), .Carry(full_adder_2_carry));
  Half_Adder half_adder_1 (.X(xor_6_out), .Y(half_adder_2_carry), .Sum(half_adder_1_sum), .Carry(half_adder_1_carry));
  xor xor_8 (xor_8_out, and_2_out, B1);
  mux mux_2 (.I0(full_adder_1_carry), .I1(half_adder_1_carry), .sign(xor_4_out), .z(mux_2_z));
  xor xor_9 (xor_9_out, full_adder_2_sum, not_1_out);
  mux mux_3 (.I0(full_adder_1_sum), .I1(half_adder_1_sum), .sign(xor_4_out), .z(mux_3_z));
  xor xor_10 (xor_10_out, and_3_out, A1);
  Half_Adder half_adder_2 (.X(xor_9_out), .Y(half_adder_3_carry), .Sum(half_adder_2_sum), .Carry(half_adder_2_carry));
  Full_Adder full_adder_3 (
    .X(xor_10_out), .Y(xor_8_out), .Z(full_adder_4_carry), .Sum(full_adder_3_sum), .Carry(full_adder_3_carry));
  xor xor_11 (xor_11_out, and_2_out, B0);
  xor xor_12 (xor_12_out, full_adder_3_sum, not_1_out);
  mux mux_4 (.I0(full_adder_2_sum), .I1(half_adder_2_sum), .sign(xor_4_out), .z(mux_4_z));
  xor xor_13 (xor_13_out, and_3_out, A0);
  Half_Adder half_adder_3 (.X(xor_12_out), .Y(half_adder_4_carry), .Sum(half_adder_3_sum), .Carry(half_adder_3_carry));
  Full_Adder full_adder_4 (
    .X(xor_13_out), .Y(xor_11_out), .Z(1'b0), .Sum(full_adder_4_sum), .Carry(full_adder_4_carry));
  xor xor_14 (xor_14_out, full_adder_4_sum, not_1_out);
  Half_Adder half_adder_4 (.X(xor_14_out), .Y(full_adder_1_carry), .Sum(half_adder_4_sum), .Carry(half_adder_4_carry));
  mux mux_5 (.I0(full_adder_3_sum), .I1(half_adder_3_sum), .sign(xor_4_out), .z(mux_5_z));
  not not_2 (not_2_out, MO_2);
  and and_4 (and_4_out, not_2_out, not_3_out);
  not not_3 (not_3_out, MO);
  mux mux_6 (.I0(full_adder_4_sum), .I1(half_adder_4_sum), .sign(xor_4_out), .z(mux_6_z));
  or or_1 (or_1_out, and_4_out, and_1_out);
  or or_2 (or_2_out, and_1_out, and_4_out);
  or or_3 (or_3_out, and_1_out, and_4_out);
  or or_4 (or_4_out, and_1_out, and_4_out);
  or or_5 (or_5_out, and_1_out, and_4_out);
  or or_6 (or_6_out, and_1_out, and_4_out);
  and and_5 (S0, or_1_out, mux_6_z);
  and and_6 (S1, or_2_out, mux_5_z);
  and and_7 (S2, or_3_out, mux_4_z);
  and and_8 (S3, or_4_out, mux_3_z);
  and and_9 (S4, mux_2_z, or_5_out);
  and and_10 (S5, mux_1_z, or_6_out);

  // Notes on the sheet:
  //   0 0 Addition
  //   Sign B
  //   Sign
endmodule
