// Logisim project 7segment.circ as structural Verilog
module a_led (
  input  A,
  input  B,
  input  C,
  input  D,
  output out_5
);

  wire and_1_out, and_2_out, and_3_out, and_4_out, and_5_out, and_6_out, and_7_out, not_1_out, not_2_out,
       not_3_out, not_4_out, or_1_out, or_2_out;

  not not_1 (not_1_out, C);
  not not_2 (not_2_out, A);
  not not_3 (not_3_out, B);
  and and_1 (and_1_out, not_2_out, C);
  and and_2 (and_2_out, not_2_out, B);
  and and_3 (and_3_out, not_3_out, not_1_out);
  not not_4 (not_4_out, D);
  and and_4 (and_4_out, A, not_1_out);
  and and_5 (and_5_out, and_2_out, D);
  and and_6 (and_6_out, and_3_out, not_4_out);
  and and_7 (and_7_out, not_3_out, and_4_out);
  or or_1 (or_1_out, and_5_out, and_6_out);
  or or_2 (or_2_out, and_1_out, or_1_out);
  or or_3 (out_5, or_2_out, and_7_out);
endmodule

module b_led (
  input  A,
  input  B,
  input  C,
  input  D,
  output out_5
);

  wire and_1_out, and_2_out, and_3_out, and_4_out, and_5_out, and_6_out, and_7_out, not_1_out, not_2_out,
       not_3_out, not_4_out, or_1_out, or_2_out;

  not not_1 (not_1_out, A);
  not not_2 (not_2_out, B);
  not not_3 (not_3_out, C);
  not not_4 (not_4_out, D);
  and and_1 (and_1_out, not_1_out, not_2_out);
  and and_2 (and_2_out, not_1_out, not_3_out);
  and and_3 (and_3_out, C, not_1_out);
  and and_4 (and_4_out, not_3_out, A);
  and and_5 (and_5_out, and_2_out, not_4_out);
  and and_6 (and_6_out, and_3_out, D);
  and and_7 (and_7_out, and_4_out, not_2_out);
  or or_1 (or_1_out, and_1_out, and_5_out);
  or or_2 (or_2_out, or_1_out, and_6_out);
  or or_3 (out_5, or_2_out, and_7_out);
endmodule

module c_led (
  input  A,
  input  B,
  input  C,
  input  D,
  output out_5
);

  wire and_1_out, and_2_out, and_3_out, and_4_out, and_5_out, and_6_out, not_1_out, not_2_out, not_3_out,
       not_4_out, or_1_out, or_2_out;

  not not_1 (not_1_out, D);
  not not_2 (not_2_out, A);
  not not_3 (not_3_out, B);
  not not_4 (not_4_out, C);
  and and_1 (and_1_out, not_2_out, B);
  and and_2 (and_2_out, not_2_out, D);
  and and_3 (and_3_out, not_3_out, not_4_out);
  and and_4 (and_4_out, A, not_3_out);
  and and_5 (and_5_out, and_4_out, not_4_out);
  and and_6 (and_6_out, and_3_out, not_1_out);
  or or_1 (or_1_out, and_1_out, and_2_out);
  or or_2 (or_2_out, or_1_out, and_6_out);
  or or_3 (out_5, or_2_out, and_5_out);
endmodule

module d_led (
  input  A,
  input  B,
  input  C,
  input  D,
  output out_5
);

  wire and_1_out, and_2_out, and_3_out, and_4_out, and_5_out, and_6_out, and_7_out, and_8_out, and_9_out,
       and_10_out, and_11_out, not_1_out, not_2_out, not_3_out, not_4_out, or_1_out, or_2_out, or_3_out;

  not not_1 (not_1_out, B);
  not not_2 (not_2_out, A);
  not not_3 (not_3_out, C);
  not not_4 (not_4_out, D);
  and and_1 (and_1_out, not_2_out, C);
  and and_2 (and_2_out, C, not_1_out);
  and and_3 (and_3_out, not_3_out, not_4_out);
  and and_4 (and_4_out, A, not_1_out);
  and and_5 (and_5_out, B, D);
  and and_6 (and_6_out, and_1_out, not_4_out);
  and and_7 (and_7_out, and_2_out, not_2_out);
  and and_8 (and_8_out, and_3_out, not_1_out);
  and and_9 (and_9_out, and_4_out, not_3_out);
  and and_10 (and_10_out, not_2_out, and_5_out);
  and and_11 (and_11_out, not_3_out, and_10_out);
  or or_1 (or_1_out, and_6_out, and_7_out);
  or or_2 (or_2_out, or_1_out, and_8_out);
  or or_3 (or_3_out, or_2_out, and_9_out);
  or or_4 (out_5, or_3_out, and_11_out);
endmodule

module e_led (
  input  A,
  input  B,
  input  C,
  input  D,
  output out_5
);

  wire and_1_out, and_2_out, and_3_out, and_4_out, not_1_out, not_2_out, not_3_out, not_4_out;

  not not_1 (not_1_out, A);
  not not_2 (not_2_out, D);
  not not_3 (not_3_out, C);
  not not_4 (not_4_out, B);
  and and_1 (and_1_out, not_1_out, not_2_out);
  and and_2 (and_2_out, not_4_out, not_2_out);
  and and_3 (and_3_out, and_1_out, C);
  and and_4 (and_4_out, and_2_out, not_3_out);
  or or_1 (out_5, and_3_out, and_4_out);
endmodule

module f_led (
  input  in_1,
  input  in_2,
  input  in_3,
  input  in_4,
  output out_5
);

  wire and_1_out, and_2_out, and_3_out, and_4_out, and_5_out, and_6_out, and_7_out, and_8_out, not_1_out,
       not_2_out, not_3_out, not_4_out, or_1_out, or_2_out;

  not not_1 (not_1_out, in_3);
  not not_2 (not_2_out, in_4);
  not not_3 (not_3_out, in_1);
  not not_4 (not_4_out, in_2);
  and and_1 (and_1_out, not_3_out, not_1_out);
  and and_2 (and_2_out, not_3_out, not_1_out);
  and and_3 (and_3_out, not_3_out, not_2_out);
  and and_4 (and_4_out, in_1, not_1_out);
  and and_5 (and_5_out, and_1_out, in_2);
  and and_6 (and_6_out, and_2_out, not_2_out);
  and and_7 (and_7_out, and_3_out, in_2);
  and and_8 (and_8_out, and_4_out, not_4_out);
  or or_1 (or_1_out, and_5_out, and_6_out);
  or or_2 (or_2_out, or_1_out, and_7_out);
  or or_3 (out_5, or_2_out, and_8_out);
endmodule

module g_led (
  input  in_1,
  input  in_2,
  input  in_3,
  input  in_4,
  output out_5
);

  wire and_1_out, and_2_out, and_3_out, and_4_out, and_5_out, and_6_out, and_7_out, and_8_out, not_1_out,
       not_2_out, not_3_out, not_4_out, or_1_out, or_2_out;

  not not_1 (not_1_out, in_4);
  not not_2 (not_2_out, in_3);
  not not_3 (not_3_out, in_1);
  not not_4 (not_4_out, in_2);
  and and_1 (and_1_out, not_3_out, in_3);
  and and_2 (and_2_out, not_3_out, in_3);
  and and_3 (and_3_out, not_3_out, not_2_out);
  and and_4 (and_4_out, in_1, not_2_out);
  and and_5 (and_5_out, and_1_out, not_1_out);
  and and_6 (and_6_out, and_2_out, not_4_out);
  and and_7 (and_7_out, and_3_out, in_2);
  and and_8 (and_8_out, and_4_out, not_4_out);
  or or_1 (or_1_out, and_5_out, and_6_out);
  or or_2 (or_2_out, or_1_out, and_7_out);
  or or_3 (out_5, or_2_out, and_8_out);
endmodule

module All_Leds (
  input  A0,
  input  A1,
  input  A2,
  input  A3,
  output A_LED,
  output B_LED,
  output C_LED,
  output D_LED,
  output E_LED,
  output F_LED,
  output G_LED
);

  b_led b_led_1 (.A(A0), .B(A1), .C(A2), .D(A3), .out_5(B_LED));
  c_led c_led_1 (.A(A0), .B(A1), .C(A2), .D(A3), .out_5(C_LED));
  d_led d_led_1 (.A(A0), .B(A1), .C(A2), .D(A3), .out_5(D_LED));
  e_led e_led_1 (.A(A0), .B(A1), .C(A2), .D(A3), .out_5(E_LED));
  f_led f_led_1 (.in_1(A0), .in_2(A1), .in_3(A2), .in_4(A3), .out_5(F_LED));
  g_led g_led_1 (.in_1(A0), .in_2(A1), .in_3(A2), .in_4(A3), .out_5(G_LED));
  a_led a_led_1 (.A(A0), .B(A1), .C(A2), .D(A3), .out_5(A_LED));
endmodule

module TEST (
  input  in_1,
  input  in_2,
  input  in_3,
  input  in_4
);

  wire all_leds_1_a_led, all_leds_1_b_led, all_leds_1_c_led, all_leds_1_d_led, all_leds_1_e_led,
       all_leds_1_f_led, all_leds_1_g_led;

  All_Leds all_leds_1 (
    .A0(in_1), .A1(in_2), .A2(in_3), .A3(in_4), .A_LED(all_leds_1_a_led), .B_LED(all_leds_1_b_led),
    .C_LED(all_leds_1_c_led), .D_LED(all_leds_1_d_led), .E_LED(all_leds_1_e_led), .F_LED(all_leds_1_f_led),
    .G_LED(all_leds_1_g_led));
  _7_Segment_Display u_7_segment_display_1 (
    .g(all_leds_1_g_led), .f(all_leds_1_f_led), .a(all_leds_1_a_led), .b(all_leds_1_b_led),
    .e(all_leds_1_e_led), .d(all_leds_1_d_led), .c(all_leds_1_c_led));  // open: dp
endmodule
