// Logisim project Addition & Subtraction.circ as structural Verilog: 5 circuits, main circuit Add/Sub
module Full_Adder (
  input  X,
  input  Y,
  input  Z,
  output Sum,
  output Carry
);

  wire and_1_out, and_2_out, xor_1_out;

  xor xor_1 (xor_1_out, X, Y);
  and and_1 (and_1_out, X, Y);
  xor xor_2 (Sum, xor_1_out, Z);
  and and_2 (and_2_out, xor_1_out, Z);
  or or_1 (Carry, and_2_out, and_1_out);
endmodule

module Half_Adder (
  input  X,
  input  Y,
  output Sum,
  output Carry
);

  xor xor_1 (Sum, X, Y);
  and and_1 (Carry, X, Y);
endmodule

module test (
  input  Mo,
  input  Mo_2,
  input  Sign_B,
  input  B3,
  input  B2,
  input  B1,
  input  B0,
  input  Sign_A,
  input  A3,
  input  A2,
  input  A1,
  input  A0,
  output S0,
  output S1,
  output S2,
  output S3,
  output S4,
  output Sign
);

  Add_Sub add_sub_1 (
    .MO(Mo_2), .MO_2(Mo), .Sign_B(Sign_B), .Sign_A(Sign_A), .B3(B3), .A3(A3), .B2(B2), .A2(A2), .B1(B1),
    .A1(A1), .B0(B0), .A0(A0), .S0(S0), .S1(S1), .S2(S2), .S3(S3), .S4(S4), .Sign(Sign));
endmodule

module mux (
  input  sign,
  input  I0,
  input  I1,
  output z
);

  wire and_1_out, and_2_out, not_1_out;

  not not_1 (not_1_out, sign);
  and and_1 (and_1_out, not_1_out, I0);
  and and_2 (and_2_out, sign, I1);
  or or_1 (z, and_1_out, and_2_out);
endmodule

module Add_Sub (
  input  MO,
  input  MO_2,
  input  Sign_B,
  input  Sign_A,
  input  B3,
  input  A3,
  input  B2,
  input  A2,
  input  B1,
  input  A1,
  input  B0,
  input  A0,
  output S0,
  output S1,
  output S2,
  output S3,
  output S4,
  output Sign
);

  wire and_1_out, and_2_out, and_3_out, full_adder_1_carry, full_adder_1_sum, full_adder_2_carry,
       full_adder_2_sum, full_adder_3_carry, full_adder_3_sum, full_adder_4_carry, full_adder_4_sum,
       half_adder_1_carry, half_adder_1_sum, half_adder_2_carry, half_adder_2_sum, half_adder_3_carry,
       half_adder_3_sum, half_adder_4_carry, half_adder_4_sum, mux_1_z, nor_1_out, nor_2_out, nor_3_out,
       nor_4_out, not_1_out, xor_1_out, xor_2_out, xor_3_out, xor_4_out, xor_5_out, xor_6_out, xor_7_out,
       xor_8_out, xor_9_out, xor_10_out, xor_11_out, xor_12_out, xor_13_out, xor_14_out;

  and and_1 (and_1_out, MO, MO_2);
  xor xor_1 (xor_1_out, and_2_out, B3);
  not not_1 (not_1_out, full_adder_1_carry);
  xor xor_2 (xor_2_out, and_1_out, Sign_B);
  xor xor_3 (xor_3_out, and_3_out, A3);
  Full_Adder full_adder_1 (
    .X(xor_3_out), .Y(xor_1_out), .Z(full_adder_2_carry), .Sum(full_adder_1_sum), .Carry(full_adder_1_carry));
  mux mux_1 (.I0(Sign_A), .I1(not_1_out), .sign(xor_4_out), .z(mux_1_z));
  xor xor_4 (xor_4_out, xor_2_out, Sign_A);
  xor xor_5 (xor_5_out, and_2_out, B2);
  xor xor_6 (xor_6_out, full_adder_1_sum, not_1_out);
  and and_2 (and_2_out, xor_2_out, xor_4_out);
  and and_3 (and_3_out, xor_4_out, Sign_A);
  xor xor_7 (xor_7_out, and_3_out, A2);
  Full_Adder full_adder_2 (
    .X(xor_7_out), .Y(xor_5_out), .Z(full_adder_3_carry), .Sum(full_adder_2_sum), .Carry(full_adder_2_carry));
  Half_Adder half_adder_1 (.X(xor_6_out), .Y(half_adder_2_carry), .Sum(half_adder_1_sum), .Carry(half_adder_1_carry));
  xor xor_8 (xor_8_out, and_2_out, B1);
  mux mux_2 (.I0(full_adder_1_carry), .I1(half_adder_1_carry), .sign(xor_4_out), .z(S4));
  xor xor_9 (xor_9_out, full_adder_2_sum, not_1_out);
  mux mux_3 (.I0(full_adder_1_sum), .I1(half_adder_1_sum), .sign(xor_4_out), .z(S3));
  xor xor_10 (xor_10_out, and_3_out, A1);
  Half_Adder half_adder_2 (.X(xor_9_out), .Y(half_adder_3_carry), .Sum(half_adder_2_sum), .Carry(half_adder_2_carry));
  Full_Adder full_adder_3 (
    .X(xor_10_out), .Y(xor_8_out), .Z(full_adder_4_carry), .Sum(full_adder_3_sum), .Carry(full_adder_3_carry));
  xor xor_11 (xor_11_out, and_2_out, B0);
  xor xor_12 (xor_12_out, full_adder_3_sum, not_1_out);
  mux mux_4 (.I0(full_adder_2_sum), .I1(half_adder_2_sum), .sign(xor_4_out), .z(S2));
  xor xor_13 (xor_13_out, and_3_out, A0);
  Half_Adder half_adder_3 (.X(xor_12_out), .Y(half_adder_4_carry), .Sum(half_adder_3_sum), .Carry(half_adder_3_carry));
  Full_Adder full_adder_4 (
    .X(xor_13_out), .Y(xor_11_out), .Z(1'b0), .Sum(full_adder_4_sum), .Carry(full_adder_4_carry));
  xor xor_14 (xor_14_out, full_adder_4_sum, not_1_out);
  Half_Adder half_adder_4 (.X(xor_14_out), .Y(full_adder_1_carry), .Sum(half_adder_4_sum), .Carry(half_adder_4_carry));
  mux mux_5 (.I0(full_adder_3_sum), .I1(half_adder_3_sum), .sign(xor_4_out), .z(S1));
  mux mux_6 (.I0(full_adder_4_sum), .I1(half_adder_4_sum), .sign(xor_4_out), .z(S0));
  nor nor_1 (nor_1_out, S3, S4);
  nor nor_2 (nor_2_out, S2, nor_1_out);
  nor nor_3 (nor_3_out, S1, nor_2_out);
  nor nor_4 (nor_4_out, S0, nor_3_out);
  and and_4 (Sign, mux_1_z, nor_4_out);

  // Notes on the sheet:
  //   0 0 Addition
  //   1 1 Subtraction
  //   Sign B
  //   Sign
endmodule
