// Logisim project division.circ as structural Verilog
module _1_1_bit_comparetor (
  input  A,
  input  B,
  output LARGER,
  output SMALLER,
  output Equal
);

  wire and_3_out, and_4_out, not_1_out, not_2_out;

  not not_1 (not_1_out, A);
  not not_2 (not_2_out, B);
  and and_1 (LARGER, A, not_2_out);
  and and_2 (SMALLER, not_1_out, B);
  and and_3 (and_3_out, not_1_out, not_2_out);
  and and_4 (and_4_out, A, B);
  or or_1 (Equal, and_3_out, and_4_out);
endmodule

module _4_bit_comparetor (
  input  a3,
  input  a2,
  input  a1,
  input  a0,
  input  b3,
  input  b2,
  input  b1,
  input  b0,
  output Larger,
  output Smaller,
  output Equal
);

  wire and_1_out, and_2_out, and_3_out, and_4_out, and_5_out, and_6_out, n1_1_bit_comparetor_1_equal,
       n1_1_bit_comparetor_1_larger, n1_1_bit_comparetor_1_smaller, n1_1_bit_comparetor_2_equal,
       n1_1_bit_comparetor_2_larger, n1_1_bit_comparetor_2_smaller, n1_1_bit_comparetor_3_equal,
       n1_1_bit_comparetor_3_larger, n1_1_bit_comparetor_3_smaller, n1_1_bit_comparetor_4_equal,
       n1_1_bit_comparetor_4_larger, n1_1_bit_comparetor_4_smaller;

  _1_1_bit_comparetor u_1_1_bit_comparetor_1 (
    .A(a3), .B(b3), .LARGER(n1_1_bit_comparetor_1_larger), .SMALLER(n1_1_bit_comparetor_1_smaller),
    .Equal(n1_1_bit_comparetor_1_equal));
  _1_1_bit_comparetor u_1_1_bit_comparetor_2 (
    .A(a2), .B(b2), .LARGER(n1_1_bit_comparetor_2_larger), .SMALLER(n1_1_bit_comparetor_2_smaller),
    .Equal(n1_1_bit_comparetor_2_equal));
  _1_1_bit_comparetor u_1_1_bit_comparetor_3 (
    .A(a1), .B(b1), .LARGER(n1_1_bit_comparetor_3_larger), .SMALLER(n1_1_bit_comparetor_3_smaller),
    .Equal(n1_1_bit_comparetor_3_equal));
  _1_1_bit_comparetor u_1_1_bit_comparetor_4 (
    .A(a0), .B(b0), .LARGER(n1_1_bit_comparetor_4_larger), .SMALLER(n1_1_bit_comparetor_4_smaller),
    .Equal(n1_1_bit_comparetor_4_equal));
  and and_1 (and_1_out, n1_1_bit_comparetor_2_larger, n1_1_bit_comparetor_1_equal);
  and and_2 (and_2_out, n1_1_bit_comparetor_1_equal, n1_1_bit_comparetor_2_equal, n1_1_bit_comparetor_3_larger);
  and and_3 (and_3_out, n1_1_bit_comparetor_1_equal, n1_1_bit_comparetor_2_equal, n1_1_bit_comparetor_3_equal, n1_1_bit_comparetor_4_larger);
  and and_4 (and_4_out, n1_1_bit_comparetor_1_equal, n1_1_bit_comparetor_2_smaller);
  and and_5 (and_5_out, n1_1_bit_comparetor_1_equal, n1_1_bit_comparetor_2_equal, n1_1_bit_comparetor_3_smaller);
  and and_6 (and_6_out, n1_1_bit_comparetor_1_equal, n1_1_bit_comparetor_2_equal, n1_1_bit_comparetor_3_equal, n1_1_bit_comparetor_4_smaller);
  and and_7 (Equal, n1_1_bit_comparetor_1_equal, n1_1_bit_comparetor_2_equal, n1_1_bit_comparetor_3_equal, n1_1_bit_comparetor_4_equal);
  or or_1 (Larger, n1_1_bit_comparetor_1_larger, and_1_out, and_2_out, and_3_out);
  or or_2 (Smaller, n1_1_bit_comparetor_1_smaller, and_4_out, and_5_out, and_6_out);
endmodule

module division (
  input  A4,
  input  A3,
  input  A2,
  input  A1,
  input  A0,
  input  B4,
  input  B3,
  input  B2,
  input  B1,
  input  B0,
  output C_SIGN,
  output C3,
  output C2,
  output out_14,
  output out_15
);

  wire division_multiplication_1_c0, division_multiplication_2_c0, division_multiplication_2_c1,
       division_multiplication_3_c0, division_multiplication_3_c1, division_multiplication_3_c2,
       division_subtraction_1_c3, division_subtraction_2_c0, division_subtraction_2_c1,
       division_subtraction_2_c2, division_subtraction_2_c3, division_subtraction_3_c1,
       division_subtraction_3_c2, division_subtraction_3_c3;

  full_adder full_adder_1 ();  // open: a, b, c, sum, carry
  _4_bit_comp_number_2 u_4_bit_comp_number_2_1 (
    .a3(1'b0), .a2(1'b0), .a1(1'b0), .a0(A3), .b3(B3), .b2(B2), .b1(B1), .b0(B0), .GREATER_OR_EQUAL(C3));
  Division_multiplication division_multiplication_1 (
    .A(C3), .B3(B3), .B2(B2), .B1(B1), .B0(B0), .C0(division_multiplication_1_c0));  // open: C3, C2, C1
  _4_bit_comp_number_2 u_4_bit_comp_number_2_2 (
    .a3(1'b0), .a2(1'b0), .a1(division_subtraction_1_c3), .a0(A2), .b3(B3), .b2(B2), .b1(B1), .b0(B0),
    .GREATER_OR_EQUAL(C2));
  _4_bit_comp_number_2 u_4_bit_comp_number_2_3 (
    .a3(1'b0), .a2(division_subtraction_2_c3), .a1(division_subtraction_2_c2), .a0(A1), .b3(B3), .b2(B2),
    .b1(B1), .b0(B0), .GREATER_OR_EQUAL(out_14));
  _4_bit_comp_number_2 u_4_bit_comp_number_2_4 (
    .a3(division_subtraction_3_c3), .a2(division_subtraction_3_c2), .a1(division_subtraction_3_c1), .a0(A0),
    .b3(B3), .b2(B2), .b1(B1), .b0(B0), .GREATER_OR_EQUAL(out_15));
  DIVISION_SUBTRACTION division_subtraction_1 (
    .b3(division_multiplication_1_c0), .a3(A3), .b2(1'b0), .a2(1'b0), .b1(1'b0), .a1(1'b0), .b0(1'b0),
    .a0(1'b0), .C3(division_subtraction_1_c3));  // open: C2, C1, C0
  Division_multiplication division_multiplication_2 (
    .A(C2), .B3(B3), .B2(B2), .B1(B1), .B0(B0), .C1(division_multiplication_2_c1),
    .C0(division_multiplication_2_c0));  // open: C3, C2
  Division_multiplication division_multiplication_3 (
    .A(out_14), .B3(B3), .B2(B2), .B1(B1), .B0(B0), .C2(division_multiplication_3_c2),
    .C1(division_multiplication_3_c1), .C0(division_multiplication_3_c0));  // open: C3
  DIVISION_SUBTRACTION division_subtraction_2 (
    .b3(division_multiplication_2_c1), .a3(division_subtraction_1_c3), .b2(division_multiplication_2_c0),
    .a2(A2), .b1(1'b0), .a1(1'b0), .b0(1'b0), .a0(1'b0), .C3(division_subtraction_2_c3),
    .C2(division_subtraction_2_c2), .C1(division_subtraction_2_c1), .C0(division_subtraction_2_c0));
  DIVISION_SUBTRACTION division_subtraction_3 (
    .b3(division_multiplication_3_c2), .a3(division_subtraction_2_c3), .b2(division_multiplication_3_c1),
    .a2(division_subtraction_2_c2), .b1(division_multiplication_3_c0), .a1(A1), .b0(1'b0), .a0(1'b0),
    .C3(division_subtraction_3_c3), .C2(division_subtraction_3_c2), .C1(division_subtraction_3_c1));  // open: C0
  xor xor_1 (C_SIGN, B4, A4);
endmodule

module _4_bit_comp_number_2 (
  input  a3,
  input  a2,
  input  a1,
  input  a0,
  input  b3,
  input  b2,
  input  b1,
  input  b0,
  output GREATER_OR_EQUAL
);

  wire and_1_out, and_2_out, and_3_out, and_4_out, n1_1_bit_comparetor_1_equal, n1_1_bit_comparetor_1_larger,
       n1_1_bit_comparetor_1_smaller, n1_1_bit_comparetor_2_equal, n1_1_bit_comparetor_2_larger,
       n1_1_bit_comparetor_2_smaller, n1_1_bit_comparetor_3_equal, n1_1_bit_comparetor_3_larger,
       n1_1_bit_comparetor_3_smaller, n1_1_bit_comparetor_4_equal, n1_1_bit_comparetor_4_larger,
       n1_1_bit_comparetor_4_smaller, or_1_out;

  _1_1_bit_comparetor u_1_1_bit_comparetor_1 (
    .A(a3), .B(b3), .LARGER(n1_1_bit_comparetor_1_larger), .SMALLER(n1_1_bit_comparetor_1_smaller),
    .Equal(n1_1_bit_comparetor_1_equal));
  _1_1_bit_comparetor u_1_1_bit_comparetor_2 (
    .A(a2), .B(b2), .LARGER(n1_1_bit_comparetor_2_larger), .SMALLER(n1_1_bit_comparetor_2_smaller),
    .Equal(n1_1_bit_comparetor_2_equal));
  _1_1_bit_comparetor u_1_1_bit_comparetor_3 (
    .A(a1), .B(b1), .LARGER(n1_1_bit_comparetor_3_larger), .SMALLER(n1_1_bit_comparetor_3_smaller),
    .Equal(n1_1_bit_comparetor_3_equal));
  _1_1_bit_comparetor u_1_1_bit_comparetor_4 (
    .A(a0), .B(b0), .LARGER(n1_1_bit_comparetor_4_larger), .SMALLER(n1_1_bit_comparetor_4_smaller),
    .Equal(n1_1_bit_comparetor_4_equal));
  and and_1 (and_1_out, n1_1_bit_comparetor_1_equal, n1_1_bit_comparetor_2_larger);
  and and_2 (and_2_out, n1_1_bit_comparetor_1_equal, n1_1_bit_comparetor_2_equal, n1_1_bit_comparetor_3_larger);
  and and_3 (and_3_out, n1_1_bit_comparetor_1_equal, n1_1_bit_comparetor_2_equal, n1_1_bit_comparetor_3_equal, n1_1_bit_comparetor_4_larger);
  and and_4 (and_4_out, n1_1_bit_comparetor_1_equal, n1_1_bit_comparetor_2_equal, n1_1_bit_comparetor_3_equal, n1_1_bit_comparetor_4_equal);
  or or_1 (or_1_out, n1_1_bit_comparetor_1_larger, and_1_out, and_2_out, and_3_out);
  or or_2 (GREATER_OR_EQUAL, or_1_out, and_4_out);
endmodule

module half_adder (
  input  a,
  input  b,
  output sum,
  output carry
);

  xor xor_1 (sum, a, b);
  and and_1 (carry, a, b);
endmodule

module full_adder (
  input  a,
  input  b,
  input  c,
  output sum,
  output carry
);

  wire half_adder_1_carry, half_adder_1_sum, half_adder_2_carry;

  half_adder half_adder_1 (.a(a), .b(b), .sum(half_adder_1_sum), .carry(half_adder_1_carry));
  half_adder half_adder_2 (.a(half_adder_1_sum), .b(c), .sum(sum), .carry(half_adder_2_carry));
  or or_1 (carry, half_adder_1_carry, half_adder_2_carry);
endmodule

module _5_bit_adder (
  input  a4,
  input  a3,
  input  a2,
  input  a1,
  input  a0,
  input  b4,
  input  b3,
  input  b2,
  input  b1,
  input  b0,
  output c5,
  output c4,
  output c3,
  output c2,
  output c1,
  output c0
);

  wire full_adder_1_carry, full_adder_2_carry, full_adder_3_carry, full_adder_4_carry;

  full_adder full_adder_1 (.a(a0), .b(b0), .c(1'b0), .sum(c0), .carry(full_adder_1_carry));
  full_adder full_adder_2 (.a(a1), .b(b1), .c(full_adder_1_carry), .sum(c1), .carry(full_adder_2_carry));
  full_adder full_adder_3 (.a(a2), .b(b2), .c(full_adder_2_carry), .sum(c2), .carry(full_adder_3_carry));
  full_adder full_adder_4 (.a(a3), .b(b3), .c(full_adder_3_carry), .sum(c3), .carry(full_adder_4_carry));
  full_adder full_adder_5 (.a(a4), .b(b4), .c(full_adder_4_carry), .sum(c4), .carry(c5));
endmodule

module _5_bit_subtractor (
  input  b4,
  input  a4,
  input  b3,
  input  a3,
  input  b2,
  input  a2,
  input  b1,
  input  a1,
  input  b0,
  input  a0,
  output out_11,
  output out_12,
  output out_13,
  output out_14,
  output out_15
);

  wire full_adder_2_carry, full_adder_3_carry, full_adder_4_carry, full_adder_5_carry, not_1_out, not_2_out,
       not_3_out, not_4_out, not_5_out, not_6_out;

  not not_1 (not_1_out, b4);
  full_adder full_adder_1 (.a(a4), .b(not_1_out), .c(full_adder_2_carry), .sum(out_11));  // open: carry
  not not_2 (not_2_out, b3);
  full_adder full_adder_2 (.a(a3), .b(not_2_out), .c(full_adder_3_carry), .sum(out_12), .carry(full_adder_2_carry));
  not not_3 (not_3_out, b2);
  full_adder full_adder_3 (.a(a2), .b(not_3_out), .c(full_adder_4_carry), .sum(out_13), .carry(full_adder_3_carry));
  not not_4 (not_4_out, b1);
  full_adder full_adder_4 (.a(a1), .b(not_4_out), .c(full_adder_5_carry), .sum(out_14), .carry(full_adder_4_carry));
  not not_5 (not_5_out, b0);
  full_adder full_adder_5 (.a(a0), .b(not_5_out), .c(not_6_out), .sum(out_15), .carry(full_adder_5_carry));
  not not_6 (not_6_out, 1'b0);
endmodule

module multiplyer (
  input  B4,
  input  B3,
  input  B2,
  input  B1,
  input  B0,
  input  A0,
  input  A1,
  input  A2,
  input  A3,
  input  A4,
  output out_11,
  output out_12,
  output out_13,
  output out_14,
  output out_15,
  output out_16,
  output out_17,
  output out_18,
  output out_19
);

  wire and_1_out, and_2_out, and_3_out, and_4_out, and_5_out, and_6_out, and_7_out, and_8_out, and_9_out,
       and_10_out, and_11_out, and_12_out, and_13_out, and_14_out, and_15_out, n5_bit_adder_2_c1,
       n5_bit_adder_2_c2, n5_bit_adder_2_c3, n5_bit_adder_2_c4, n5_bit_adder_3_c1, n5_bit_adder_3_c2,
       n5_bit_adder_3_c3, n5_bit_adder_3_c4;

  xor xor_1 (out_11, A4, B4);
  and and_1 (and_1_out, A1, B3);
  and and_2 (and_2_out, A2, B3);
  and and_3 (and_3_out, A3, B3);
  and and_4 (and_4_out, A1, B2);
  and and_5 (and_5_out, A2, B2);
  and and_6 (and_6_out, A3, B2);
  _5_bit_adder u_5_bit_adder_1 (
    .a4(1'b0), .b4(1'b0), .a3(and_3_out), .b3(n5_bit_adder_3_c4), .b2(n5_bit_adder_3_c3), .a2(and_6_out),
    .b1(and_9_out), .a1(n5_bit_adder_3_c2), .b0(and_12_out), .a0(n5_bit_adder_3_c1), .c4(out_12),
    .c3(out_13), .c2(out_14), .c1(out_15), .c0(out_16));  // open: c5
  and and_7 (and_7_out, A1, B1);
  _5_bit_adder u_5_bit_adder_2 (
    .a4(1'b0), .b4(1'b0), .a3(and_1_out), .b3(1'b0), .b2(and_10_out), .a2(and_4_out), .b1(and_7_out),
    .a1(and_14_out), .b0(and_13_out), .a0(and_15_out), .c4(n5_bit_adder_2_c4), .c3(n5_bit_adder_2_c3),
    .c2(n5_bit_adder_2_c2), .c1(n5_bit_adder_2_c1), .c0(out_18));  // open: c5
  and and_8 (and_8_out, A2, B1);
  _5_bit_adder u_5_bit_adder_3 (
    .a4(1'b0), .b4(1'b0), .a3(and_2_out), .b3(n5_bit_adder_2_c4), .b2(n5_bit_adder_2_c3), .a2(and_5_out),
    .b1(and_8_out), .a1(n5_bit_adder_2_c2), .b0(and_11_out), .a0(n5_bit_adder_2_c1), .c4(n5_bit_adder_3_c4),
    .c3(n5_bit_adder_3_c3), .c2(n5_bit_adder_3_c2), .c1(n5_bit_adder_3_c1), .c0(out_17));  // open: c5
  and and_9 (and_9_out, A3, B1);
  and and_10 (and_10_out, A0, B3);
  and and_11 (and_11_out, A2, B0);
  and and_12 (and_12_out, A3, B0);
  and and_13 (and_13_out, A1, B0);
  and and_14 (and_14_out, A0, B2);
  and and_15 (and_15_out, A0, B1);
  and and_16 (out_19, A0, B0);
endmodule

module circuit (
  input  [4:0] in_1,
  input  [4:0] in_2,
  output [4:0] out_3
);

  division division_1 (
    .A4(in_1[4]), .A3(in_1[3]), .A2(in_1[2]), .A1(in_1[1]), .A0(in_1[0]), .B4(in_2[4]), .B3(in_2[3]),
    .B2(in_2[2]), .B1(in_2[1]), .B0(in_2[0]), .C_SIGN(out_3[4]), .C3(out_3[3]), .C2(out_3[2]),
    .out_14(out_3[1]), .out_15(out_3[0]));
endmodule

module Division_multiplication (
  input  B3,
  input  B2,
  input  B1,
  input  B0,
  input  A,
  output C3,
  output C2,
  output C1,
  output C0
);

  and and_1 (C3, A, B3);
  and and_2 (C2, A, B2);
  and and_3 (C1, A, B1);
  and and_4 (C0, A, B0);
endmodule

module DIVISION_SUBTRACTION (
  input  b3,
  input  a3,
  input  b2,
  input  a2,
  input  b1,
  input  a1,
  input  b0,
  input  a0,
  output C3,
  output C2,
  output C1,
  output C0
);

  wire full_adder_2_carry, full_adder_3_carry, full_adder_4_carry, not_1_out, not_2_out, not_3_out,
       not_4_out, not_5_out;

  not not_1 (not_1_out, b3);
  full_adder full_adder_1 (.a(a3), .b(not_1_out), .c(full_adder_2_carry), .sum(C3));  // open: carry
  not not_2 (not_2_out, b2);
  full_adder full_adder_2 (.a(a2), .b(not_2_out), .c(full_adder_3_carry), .sum(C2), .carry(full_adder_2_carry));
  not not_3 (not_3_out, b1);
  full_adder full_adder_3 (.a(a1), .b(not_3_out), .c(full_adder_4_carry), .sum(C1), .carry(full_adder_3_carry));
  not not_4 (not_4_out, b0);
  full_adder full_adder_4 (.a(a0), .b(not_4_out), .c(not_5_out), .sum(C0), .carry(full_adder_4_carry));
  not not_5 (not_5_out, 1'b0);
endmodule

module _7_segment (
  input  x3,
  input  x2,
  input  x1,
  input  x0,
  output a,
  output b,
  output c,
  output d,
  output e,
  output f,
  output g
);

  wire and_1_out, and_2_out, and_3_out, and_4_out, and_5_out, and_6_out, and_7_out, and_8_out, and_9_out,
       not_1_out, not_2_out, not_3_out, not_4_out, or_1_out, or_2_out, or_3_out, or_4_out, or_6_out,
       or_7_out, or_8_out, or_12_out, or_13_out, or_14_out, or_15_out;

  not not_1 (not_1_out, x3);
  not not_2 (not_2_out, x2);
  not not_3 (not_3_out, x1);
  not not_4 (not_4_out, x0);
  and and_1 (and_1_out, x2, x1);
  and and_2 (and_2_out, x2, not_4_out);
  and and_3 (and_3_out, x2, x0);
  and and_4 (and_4_out, not_2_out, not_4_out);
  and and_5 (and_5_out, x1, x0);
  and and_6 (and_6_out, not_3_out, not_4_out);
  and and_7 (and_7_out, x1, not_4_out);
  and and_8 (and_8_out, not_2_out, x1);
  and and_9 (and_9_out, x0, and_1_out);
  or or_1 (or_1_out, and_3_out, and_4_out);
  or or_2 (or_2_out, and_5_out, and_6_out);
  or or_3 (or_3_out, x2, not_3_out);
  or or_4 (or_4_out, and_7_out, and_8_out);
  or or_5 (e, and_7_out, and_4_out);
  or or_6 (or_6_out, and_1_out, and_2_out);
  or or_7 (or_7_out, and_1_out, and_8_out);
  or or_8 (or_8_out, or_1_out, x3);
  or or_9 (b, or_2_out, not_2_out);
  or or_10 (a, or_8_out, x1);
  or or_11 (c, or_3_out, x0);
  or or_12 (or_12_out, or_4_out, x3);
  or or_13 (or_13_out, or_12_out, and_9_out);
  or or_14 (or_14_out, or_6_out, x3);
  or or_15 (or_15_out, or_7_out, x3);
  or or_16 (d, or_13_out, and_4_out);
  or or_17 (f, or_14_out, and_6_out);
  or or_18 (g, or_15_out, and_7_out);
endmodule

module test (
  input  in_1,
  input  in_2,
  input  in_3,
  input  in_4,
  input  in_5,
  input  in_6,
  input  in_7,
  input  in_8,
  input  in_9,
  input  in_10,
  input  in_11,
  input  in_12,
  input  in_13,
  input  in_14,
  output out_15,
  output out_16,
  output out_17,
  output out_18,
  output out_19,
  output out_20,
  output out_21,
  output out_22,
  output out_23,
  output out_24,
  output out_25,
  output out_26
);

  wire n7_segment_1_a, n7_segment_1_b, n7_segment_1_c, n7_segment_1_d, n7_segment_1_e, n7_segment_1_f,
       n7_segment_1_g;

  multiplyer multiplyer_1 (
    .A0(in_10), .A1(in_11), .A2(in_12), .A3(in_13), .A4(in_14), .B4(in_8), .B3(in_6), .B2(in_5), .B1(in_7),
    .B0(in_9), .out_11(out_15), .out_12(out_16), .out_13(out_17), .out_14(out_18), .out_15(out_19),
    .out_16(out_20), .out_17(out_21), .out_18(out_22), .out_19(out_23));
  _7_segment u_7_segment_1 (
    .x3(in_1), .x2(in_2), .x1(in_3), .x0(in_4), .a(n7_segment_1_a), .b(n7_segment_1_b), .c(n7_segment_1_c),
    .d(n7_segment_1_d), .e(n7_segment_1_e), .f(n7_segment_1_f), .g(n7_segment_1_g));
  _7_Segment_Display u_7_segment_display_1 (
    .g(n7_segment_1_g), .f(n7_segment_1_f), .a(n7_segment_1_a), .b(n7_segment_1_b), .e(n7_segment_1_e),
    .d(n7_segment_1_d), .c(n7_segment_1_c));  // open: dp
endmodule
