// Logisim project multiplication.circ as structural Verilog: 3 circuits, main circuit main
module main (
  input  A4,
  input  A3,
  input  A2,
  input  A1,
  input  A0,
  input  B0,
  input  B1,
  input  B2,
  input  B3,
  input  B4,
  output out_11,
  output out_12,
  output out_13,
  output out_14,
  output out_15,
  output out_16,
  output out_17,
  output out_18,
  output out_19
);

  wire and_1_out, and_2_out, and_3_out, and_4_out, and_5_out, and_6_out, and_7_out, and_8_out, and_9_out,
       and_10_out, and_11_out, and_12_out, and_13_out, and_14_out, and_15_out, fa_2_out_4, fa_2_out_5,
       fa_3_out_4, fa_3_out_5, fa_4_out_5, fa_5_out_4, fa_5_out_5, fa_6_out_4, fa_6_out_5, fa_7_out_5,
       fa_8_out_4, fa_8_out_5, ha_1_out_3, ha_1_out_4, ha_2_out_4, ha_3_out_4, ha_4_out_4;

  FA fa_1 (.in_1(fa_4_out_5), .in_2(and_1_out), .in_3(fa_2_out_5), .out_4(out_13), .out_5(out_12));
  FA fa_2 (.in_1(fa_3_out_5), .in_2(and_2_out), .in_3(ha_1_out_4), .out_4(fa_2_out_4), .out_5(fa_2_out_5));
  and and_1 (and_1_out, A3, B3);
  xor xor_1 (out_11, A4, B4);
  and and_2 (and_2_out, A3, B2);
  HA ha_1 (.in_1(fa_5_out_5), .in_2(and_3_out), .out_3(ha_1_out_3), .out_4(ha_1_out_4));
  FA fa_3 (.in_1(fa_6_out_5), .in_2(and_6_out), .in_3(ha_1_out_3), .out_4(fa_3_out_4), .out_5(fa_3_out_5));
  FA fa_4 (.in_1(fa_7_out_5), .in_2(and_4_out), .in_3(fa_2_out_4), .out_4(out_14), .out_5(fa_4_out_5));
  and and_3 (and_3_out, A3, B1);
  and and_4 (and_4_out, A2, B3);
  and and_5 (and_5_out, A3, B0);
  and and_6 (and_6_out, A2, B2);
  FA fa_5 (.in_1(fa_8_out_5), .in_2(and_7_out), .in_3(and_5_out), .out_4(fa_5_out_4), .out_5(fa_5_out_5));
  FA fa_6 (.in_1(ha_3_out_4), .in_2(and_9_out), .in_3(fa_5_out_4), .out_4(fa_6_out_4), .out_5(fa_6_out_5));
  FA fa_7 (.in_1(ha_2_out_4), .in_2(and_8_out), .in_3(fa_3_out_4), .out_4(out_15), .out_5(fa_7_out_5));
  and and_7 (and_7_out, A2, B1);
  and and_8 (and_8_out, A1, B3);
  and and_9 (and_9_out, A1, B2);
  and and_10 (and_10_out, A2, B0);
  HA ha_2 (.in_1(and_12_out), .in_2(fa_6_out_4), .out_3(out_16), .out_4(ha_2_out_4));
  and and_11 (and_11_out, A1, B1);
  FA fa_8 (.in_1(ha_4_out_4), .in_2(and_11_out), .in_3(and_10_out), .out_4(fa_8_out_4), .out_5(fa_8_out_5));
  HA ha_3 (.in_1(and_14_out), .in_2(fa_8_out_4), .out_3(out_17), .out_4(ha_3_out_4));
  and and_12 (and_12_out, A0, B3);
  and and_13 (and_13_out, A1, B0);
  and and_14 (and_14_out, A0, B2);
  and and_15 (and_15_out, A0, B1);
  HA ha_4 (.in_1(and_15_out), .in_2(and_13_out), .out_3(out_18), .out_4(ha_4_out_4));
  and and_16 (out_19, A0, B0);

  // Notes on the sheet:
  //   P8
  //   P7
  //   P6
  //   P5
  //   P4
  //   P3
  //   P2
  //   P1
  //   P0
endmodule

module HA (
  input  in_1,
  input  in_2,
  output out_3,
  output out_4
);

  xor xor_1 (out_3, in_1, in_2);
  and and_1 (out_4, in_1, in_2);
endmodule

module FA (
  input  in_1,
  input  in_2,
  input  in_3,
  output out_4,
  output out_5
);

  wire and_1_out, and_2_out, xor_1_out;

  and and_1 (and_1_out, in_1, in_2);
  xor xor_1 (xor_1_out, in_1, in_2);
  xor xor_2 (out_4, xor_1_out, in_3);
  and and_2 (and_2_out, xor_1_out, in_3);
  or or_1 (out_5, and_2_out, and_1_out);
endmodule
